# Fritzing sketch seven-segm-circuit (saved by Fritzing 0.9.2b)
circuit board: 8.46667cm x 5.64444cm
breadboards: 1

parts:
  Q1 = NPN-Transistor [package="TO92 [THT]"]
  U1 = 74HC595 [package="DIP16 [THT]"]
  LED2 = LED - 5mm [color="White (4500K)" current=20mA package="5 mm [THT]"]
  LED3 = LED - 5mm [color="White (4500K)" current=20mA package="5 mm [THT]"]
  LED4 = LED - 5mm [color="White (4500K)" current=20mA package="5 mm [THT]"]
  LED5 = LED - 5mm [color="White (4500K)" current=20mA package="5 mm [THT]"]
  LED6 = LED - 5mm [color="White (4500K)" current=20mA package="5 mm [THT]"]
  LED7 = LED - 5mm [color="White (4500K)" current=20mA package="5 mm [THT]"]
  R1 = Resistor [tolerance=±5% resistance=300 package=THT]
  R2 = Resistor [tolerance=±5% resistance=300 package=THT]
  LED8 = LED - 5mm [color="White (4500K)" current=20mA package="5 mm [THT]"]
  LED9 = LED - 5mm [color="White (4500K)" current=20mA package="5 mm [THT]"]
  LED10 = LED - 5mm [color="White (4500K)" current=20mA package="5 mm [THT]"]
  R3 = Resistor [tolerance=±5% resistance=300 package=THT]
  R4 = Resistor [tolerance=±5% resistance=1k package=THT]
  U2 = atmega168 [package=dip]
  XTAL1 = Crystal [frequency="16 Mhz" package=THT]
  C1 = Ceramic Capacitor [capacitance=22pF package="100 mil [THT, multilayer]"]
  C2 = Ceramic Capacitor [capacitance=22pF package="100 mil [THT, multilayer]"]
  U3 = Voltage Regulator - 5V [package="TO220 [THT]"]
  S1 = Pushbutton [package="[THT]"]
  R5 = Resistor [tolerance=±5% resistance=10k package=THT]
  Q3 = NPN-Transistor [package="TO92 [THT]"]
  LED15 = LED - 5mm [color="White (4500K)" current=20mA package="5 mm [THT]"]
  LED16 = LED - 5mm [color="White (4500K)" current=20mA package="5 mm [THT]"]
  LED17 = LED - 5mm [color="White (4500K)" current=20mA package="5 mm [THT]"]
  LED18 = LED - 5mm [color="White (4500K)" current=20mA package="5 mm [THT]"]
  LED19 = LED - 5mm [color="White (4500K)" current=20mA package="5 mm [THT]"]
  LED20 = LED - 5mm [color="White (4500K)" current=20mA package="5 mm [THT]"]
  LED21 = LED - 5mm [color="White (4500K)" current=20mA package="5 mm [THT]"]
  LED22 = LED - 5mm [color="White (4500K)" current=20mA package="5 mm [THT]"]
  LED23 = LED - 5mm [color="White (4500K)" current=20mA package="5 mm [THT]"]
  R8 = Resistor [tolerance=±5% resistance=300 package=THT]
  R9 = Resistor [tolerance=±5% resistance=300 package=THT]
  R10 = Resistor [tolerance=±5% resistance=300 package=THT]
  R11 = Resistor [tolerance=±5% resistance=1k package=THT]
  Q4 = NPN-Transistor [package="TO92 [THT]"]
  LED24 = LED - 5mm [color="White (4500K)" current=20mA package="5 mm [THT]"]
  LED25 = LED - 5mm [color="White (4500K)" current=20mA package="5 mm [THT]"]
  LED26 = LED - 5mm [color="White (4500K)" current=20mA package="5 mm [THT]"]
  LED27 = LED - 5mm [color="White (4500K)" current=20mA package="5 mm [THT]"]
  LED28 = LED - 5mm [color="White (4500K)" current=20mA package="5 mm [THT]"]
  LED29 = LED - 5mm [color="White (4500K)" current=20mA package="5 mm [THT]"]
  LED30 = LED - 5mm [color="White (4500K)" current=20mA package="5 mm [THT]"]
  LED31 = LED - 5mm [color="White (4500K)" current=20mA package="5 mm [THT]"]
  LED32 = LED - 5mm [color="White (4500K)" current=20mA package="5 mm [THT]"]
  R12 = Resistor [tolerance=±5% resistance=300 package=THT]
  R13 = Resistor [tolerance=±5% resistance=300 package=THT]
  R14 = Resistor [tolerance=±5% resistance=300 package=THT]
  R15 = Resistor [tolerance=±5% resistance=1k package=THT]
  Q5 = NPN-Transistor [package="TO92 [THT]"]
  LED33 = LED - 5mm [color="White (4500K)" current=20mA package="5 mm [THT]"]
  LED34 = LED - 5mm [color="White (4500K)" current=20mA package="5 mm [THT]"]
  LED35 = LED - 5mm [color="White (4500K)" current=20mA package="5 mm [THT]"]
  LED36 = LED - 5mm [color="White (4500K)" current=20mA package="5 mm [THT]"]
  LED37 = LED - 5mm [color="White (4500K)" current=20mA package="5 mm [THT]"]
  LED38 = LED - 5mm [color="White (4500K)" current=20mA package="5 mm [THT]"]
  LED39 = LED - 5mm [color="White (4500K)" current=20mA package="5 mm [THT]"]
  LED40 = LED - 5mm [color="White (4500K)" current=20mA package="5 mm [THT]"]
  LED41 = LED - 5mm [color="White (4500K)" current=20mA package="5 mm [THT]"]
  R16 = Resistor [tolerance=±5% resistance=300 package=THT]
  R17 = Resistor [tolerance=±5% resistance=300 package=THT]
  R18 = Resistor [tolerance=±5% resistance=300 package=THT]
  Q6 = NPN-Transistor [package="TO92 [THT]"]
  LED42 = LED - 5mm [color="White (4500K)" current=20mA package="5 mm [THT]"]
  LED43 = LED - 5mm [color="White (4500K)" current=20mA package="5 mm [THT]"]
  LED44 = LED - 5mm [color="White (4500K)" current=20mA package="5 mm [THT]"]
  LED45 = LED - 5mm [color="White (4500K)" current=20mA package="5 mm [THT]"]
  LED46 = LED - 5mm [color="White (4500K)" current=20mA package="5 mm [THT]"]
  LED47 = LED - 5mm [color="White (4500K)" current=20mA package="5 mm [THT]"]
  LED48 = LED - 5mm [color="White (4500K)" current=20mA package="5 mm [THT]"]
  LED49 = LED - 5mm [color="White (4500K)" current=20mA package="5 mm [THT]"]
  LED50 = LED - 5mm [color="White (4500K)" current=20mA package="5 mm [THT]"]
  R19 = Resistor [tolerance=±5% resistance=300 package=THT]
  R20 = Resistor [tolerance=±5% resistance=300 package=THT]
  R21 = Resistor [tolerance=±5% resistance=300 package=THT]
  Q7 = NPN-Transistor [package="TO92 [THT]"]
  LED51 = LED - 5mm [color="White (4500K)" current=20mA package="5 mm [THT]"]
  LED52 = LED - 5mm [color="White (4500K)" current=20mA package="5 mm [THT]"]
  LED53 = LED - 5mm [color="White (4500K)" current=20mA package="5 mm [THT]"]
  LED54 = LED - 5mm [color="White (4500K)" current=20mA package="5 mm [THT]"]
  LED55 = LED - 5mm [color="White (4500K)" current=20mA package="5 mm [THT]"]
  LED56 = LED - 5mm [color="White (4500K)" current=20mA package="5 mm [THT]"]
  LED57 = LED - 5mm [color="White (4500K)" current=20mA package="5 mm [THT]"]
  LED58 = LED - 5mm [color="White (4500K)" current=20mA package="5 mm [THT]"]
  LED59 = LED - 5mm [color="White (4500K)" current=20mA package="5 mm [THT]"]
  R22 = Resistor [tolerance=±5% resistance=300 package=THT]
  R23 = Resistor [tolerance=±5% resistance=300 package=THT]
  R24 = Resistor [tolerance=±5% resistance=300 package=THT]
  Q8 = NPN-Transistor [package="TO92 [THT]"]
  LED60 = LED - 5mm [color="White (4500K)" current=20mA package="5 mm [THT]"]
  LED61 = LED - 5mm [color="White (4500K)" current=20mA package="5 mm [THT]"]
  LED62 = LED - 5mm [color="White (4500K)" current=20mA package="5 mm [THT]"]
  LED63 = LED - 5mm [color="White (4500K)" current=20mA package="5 mm [THT]"]
  LED64 = LED - 5mm [color="White (4500K)" current=20mA package="5 mm [THT]"]
  LED65 = LED - 5mm [color="White (4500K)" current=20mA package="5 mm [THT]"]
  LED66 = LED - 5mm [color="White (4500K)" current=20mA package="5 mm [THT]"]
  LED67 = LED - 5mm [color="White (4500K)" current=20mA package="5 mm [THT]"]
  LED68 = LED - 5mm [color="White (4500K)" current=20mA package="5 mm [THT]"]
  R25 = Resistor [tolerance=±5% resistance=300 package=THT]
  R26 = Resistor [tolerance=±5% resistance=300 package=THT]
  R27 = Resistor [tolerance=±5% resistance=300 package=THT]
  Q9 = NPN-Transistor [package="TO92 [THT]"]
  LED72 = LED - 5mm [color="White (4500K)" current=20mA package="5 mm [THT]"]
  LED73 = LED - 5mm [color="White (4500K)" current=20mA package="5 mm [THT]"]
  LED74 = LED - 5mm [color="White (4500K)" current=20mA package="5 mm [THT]"]
  LED76 = LED - 5mm [color="White (4500K)" current=20mA package="5 mm [THT]"]
  R29 = Resistor [tolerance=±5% resistance=300 package=THT]
  R30 = Resistor [tolerance=±5% resistance=300 package=THT]
  U4 = 74HC595 [package="DIP16 [THT]"]
  C3 = Ceramic Capacitor [capacitance=1µF package="100 mil [THT, multilayer]"]
  U5 = 74HC595 [package="DIP16 [THT]"]
  U6 = 74HC595 [package="DIP16 [THT]"]
  IC1 = IC, DIP package, 8 pins [chip_label="RTC clock"]
  R31 = Resistor [tolerance=±5% resistance=1k package=THT]
  R32 = Resistor [tolerance=±5% resistance=1k package=THT]
  R33 = Resistor [tolerance=±5% resistance=1k package=THT]
  R34 = Resistor [tolerance=±5% resistance=1k package=THT]
  R35 = Resistor [tolerance=±5% resistance=1k package=THT]
  Q10 = NPN-Transistor [package="TO92 [THT]"]
  LED77 = LED - 5mm [color="White (4500K)" current=20mA package="5 mm [THT]"]
  LED78 = LED - 5mm [color="White (4500K)" current=20mA package="5 mm [THT]"]
  LED79 = LED - 5mm [color="White (4500K)" current=20mA package="5 mm [THT]"]
  LED80 = LED - 5mm [color="White (4500K)" current=20mA package="5 mm [THT]"]
  LED81 = LED - 5mm [color="White (4500K)" current=20mA package="5 mm [THT]"]
  LED82 = LED - 5mm [color="White (4500K)" current=20mA package="5 mm [THT]"]
  LED83 = LED - 5mm [color="White (4500K)" current=20mA package="5 mm [THT]"]
  LED84 = LED - 5mm [color="White (4500K)" current=20mA package="5 mm [THT]"]
  LED85 = LED - 5mm [color="White (4500K)" current=20mA package="5 mm [THT]"]
  R36 = Resistor [tolerance=±5% resistance=300 package=THT]
  R37 = Resistor [tolerance=±5% resistance=300 package=THT]
  R38 = Resistor [tolerance=±5% resistance=300 package=THT]
  R39 = Resistor [tolerance=±5% resistance=1k package=THT]
  Q11 = NPN-Transistor [package="TO92 [THT]"]
  LED86 = LED - 5mm [color="White (4500K)" current=20mA package="5 mm [THT]"]
  LED87 = LED - 5mm [color="White (4500K)" current=20mA package="5 mm [THT]"]
  LED88 = LED - 5mm [color="White (4500K)" current=20mA package="5 mm [THT]"]
  LED89 = LED - 5mm [color="White (4500K)" current=20mA package="5 mm [THT]"]
  LED90 = LED - 5mm [color="White (4500K)" current=20mA package="5 mm [THT]"]
  LED91 = LED - 5mm [color="White (4500K)" current=20mA package="5 mm [THT]"]
  LED92 = LED - 5mm [color="White (4500K)" current=20mA package="5 mm [THT]"]
  LED93 = LED - 5mm [color="White (4500K)" current=20mA package="5 mm [THT]"]
  LED94 = LED - 5mm [color="White (4500K)" current=20mA package="5 mm [THT]"]
  R40 = Resistor [tolerance=±5% resistance=300 package=THT]
  R41 = Resistor [tolerance=±5% resistance=300 package=THT]
  R42 = Resistor [tolerance=±5% resistance=300 package=THT]
  R43 = Resistor [tolerance=±5% resistance=1k package=THT]
  Q12 = NPN-Transistor [package="TO92 [THT]"]
  Q13 = NPN-Transistor [package="TO92 [THT]"]
  Q14 = NPN-Transistor [package="TO92 [THT]"]
  Q15 = NPN-Transistor [package="TO92 [THT]"]
  Q16 = NPN-Transistor [package="TO92 [THT]"]
  Q17 = NPN-Transistor [package="TO92 [THT]"]
  LED95 = LED - 5mm [color="White (4500K)" current=20mA package="5 mm [THT]"]
  LED96 = LED - 5mm [color="White (4500K)" current=20mA package="5 mm [THT]"]
  LED97 = LED - 5mm [color="White (4500K)" current=20mA package="5 mm [THT]"]
  LED98 = LED - 5mm [color="White (4500K)" current=20mA package="5 mm [THT]"]
  LED99 = LED - 5mm [color="White (4500K)" current=20mA package="5 mm [THT]"]
  LED100 = LED - 5mm [color="White (4500K)" current=20mA package="5 mm [THT]"]
  LED101 = LED - 5mm [color="White (4500K)" current=20mA package="5 mm [THT]"]
  LED102 = LED - 5mm [color="White (4500K)" current=20mA package="5 mm [THT]"]
  LED103 = LED - 5mm [color="White (4500K)" current=20mA package="5 mm [THT]"]
  LED104 = LED - 5mm [color="White (4500K)" current=20mA package="5 mm [THT]"]
  LED105 = LED - 5mm [color="White (4500K)" current=20mA package="5 mm [THT]"]
  LED106 = LED - 5mm [color="White (4500K)" current=20mA package="5 mm [THT]"]
  LED107 = LED - 5mm [color="White (4500K)" current=20mA package="5 mm [THT]"]
  LED108 = LED - 5mm [color="White (4500K)" current=20mA package="5 mm [THT]"]
  LED109 = LED - 5mm [color="White (4500K)" current=20mA package="5 mm [THT]"]
  LED110 = LED - 5mm [color="White (4500K)" current=20mA package="5 mm [THT]"]
  LED111 = LED - 5mm [color="White (4500K)" current=20mA package="5 mm [THT]"]
  LED112 = LED - 5mm [color="White (4500K)" current=20mA package="5 mm [THT]"]
  LED113 = LED - 5mm [color="White (4500K)" current=20mA package="5 mm [THT]"]
  LED114 = LED - 5mm [color="White (4500K)" current=20mA package="5 mm [THT]"]
  LED115 = LED - 5mm [color="White (4500K)" current=20mA package="5 mm [THT]"]
  LED116 = LED - 5mm [color="White (4500K)" current=20mA package="5 mm [THT]"]
  LED117 = LED - 5mm [color="White (4500K)" current=20mA package="5 mm [THT]"]
  LED118 = LED - 5mm [color="White (4500K)" current=20mA package="5 mm [THT]"]
  LED119 = LED - 5mm [color="White (4500K)" current=20mA package="5 mm [THT]"]
  LED120 = LED - 5mm [color="White (4500K)" current=20mA package="5 mm [THT]"]
  LED121 = LED - 5mm [color="White (4500K)" current=20mA package="5 mm [THT]"]
  LED122 = LED - 5mm [color="White (4500K)" current=20mA package="5 mm [THT]"]
  LED123 = LED - 5mm [color="White (4500K)" current=20mA package="5 mm [THT]"]
  LED124 = LED - 5mm [color="White (4500K)" current=20mA package="5 mm [THT]"]
  LED125 = LED - 5mm [color="White (4500K)" current=20mA package="5 mm [THT]"]
  LED126 = LED - 5mm [color="White (4500K)" current=20mA package="5 mm [THT]"]
  LED127 = LED - 5mm [color="White (4500K)" current=20mA package="5 mm [THT]"]
  LED128 = LED - 5mm [color="White (4500K)" current=20mA package="5 mm [THT]"]
  LED129 = LED - 5mm [color="White (4500K)" current=20mA package="5 mm [THT]"]
  LED130 = LED - 5mm [color="White (4500K)" current=20mA package="5 mm [THT]"]
  LED131 = LED - 5mm [color="White (4500K)" current=20mA package="5 mm [THT]"]
  LED132 = LED - 5mm [color="White (4500K)" current=20mA package="5 mm [THT]"]
  LED133 = LED - 5mm [color="White (4500K)" current=20mA package="5 mm [THT]"]
  LED134 = LED - 5mm [color="White (4500K)" current=20mA package="5 mm [THT]"]
  LED135 = LED - 5mm [color="White (4500K)" current=20mA package="5 mm [THT]"]
  LED136 = LED - 5mm [color="White (4500K)" current=20mA package="5 mm [THT]"]
  LED137 = LED - 5mm [color="White (4500K)" current=20mA package="5 mm [THT]"]
  LED138 = LED - 5mm [color="White (4500K)" current=20mA package="5 mm [THT]"]
  LED139 = LED - 5mm [color="White (4500K)" current=20mA package="5 mm [THT]"]
  LED140 = LED - 5mm [color="White (4500K)" current=20mA package="5 mm [THT]"]
  LED141 = LED - 5mm [color="White (4500K)" current=20mA package="5 mm [THT]"]
  LED142 = LED - 5mm [color="White (4500K)" current=20mA package="5 mm [THT]"]
  LED143 = LED - 5mm [color="White (4500K)" current=20mA package="5 mm [THT]"]
  R44 = Resistor [tolerance=±5% resistance=300 package=THT]
  R45 = Resistor [tolerance=±5% resistance=300 package=THT]
  R46 = Resistor [tolerance=±5% resistance=300 package=THT]
  R47 = Resistor [tolerance=±5% resistance=300 package=THT]
  R48 = Resistor [tolerance=±5% resistance=300 package=THT]
  R49 = Resistor [tolerance=±5% resistance=300 package=THT]
  R50 = Resistor [tolerance=±5% resistance=300 package=THT]
  R51 = Resistor [tolerance=±5% resistance=300 package=THT]
  R52 = Resistor [tolerance=±5% resistance=300 package=THT]
  R53 = Resistor [tolerance=±5% resistance=300 package=THT]
  R54 = Resistor [tolerance=±5% resistance=300 package=THT]
  R55 = Resistor [tolerance=±5% resistance=300 package=THT]
  R56 = Resistor [tolerance=±5% resistance=300 package=THT]
  R57 = Resistor [tolerance=±5% resistance=300 package=THT]
  R58 = Resistor [tolerance=±5% resistance=300 package=THT]
  R59 = Resistor [tolerance=±5% resistance=300 package=THT]
  R60 = Resistor [tolerance=±5% resistance=300 package=THT]
  R61 = Resistor [tolerance=±5% resistance=1k package=THT]
  R62 = Resistor [tolerance=±5% resistance=1k package=THT]
  R63 = Resistor [tolerance=±5% resistance=1k package=THT]
  R64 = Resistor [tolerance=±5% resistance=1k package=THT]
  R65 = Resistor [tolerance=±5% resistance=1k package=THT]
  R66 = Resistor [tolerance=±5% resistance=1k package=THT]
  Q18 = NPN-Transistor [package="TO92 [THT]"]
  Q19 = NPN-Transistor [package="TO92 [THT]"]
  Q20 = NPN-Transistor [package="TO92 [THT]"]
  Q21 = NPN-Transistor [package="TO92 [THT]"]
  Q22 = NPN-Transistor [package="TO92 [THT]"]
  Q23 = NPN-Transistor [package="TO92 [THT]"]
  Q24 = NPN-Transistor [package="TO92 [THT]"]
  Q25 = NPN-Transistor [package="TO92 [THT]"]
  LED144 = LED - 5mm [color="White (4500K)" current=20mA package="5 mm [THT]"]
  LED145 = LED - 5mm [color="White (4500K)" current=20mA package="5 mm [THT]"]
  LED146 = LED - 5mm [color="White (4500K)" current=20mA package="5 mm [THT]"]
  LED147 = LED - 5mm [color="White (4500K)" current=20mA package="5 mm [THT]"]
  LED148 = LED - 5mm [color="White (4500K)" current=20mA package="5 mm [THT]"]
  LED149 = LED - 5mm [color="White (4500K)" current=20mA package="5 mm [THT]"]
  LED150 = LED - 5mm [color="White (4500K)" current=20mA package="5 mm [THT]"]
  LED151 = LED - 5mm [color="White (4500K)" current=20mA package="5 mm [THT]"]
  LED152 = LED - 5mm [color="White (4500K)" current=20mA package="5 mm [THT]"]
  LED153 = LED - 5mm [color="White (4500K)" current=20mA package="5 mm [THT]"]
  LED154 = LED - 5mm [color="White (4500K)" current=20mA package="5 mm [THT]"]
  LED155 = LED - 5mm [color="White (4500K)" current=20mA package="5 mm [THT]"]
  LED156 = LED - 5mm [color="White (4500K)" current=20mA package="5 mm [THT]"]
  LED157 = LED - 5mm [color="White (4500K)" current=20mA package="5 mm [THT]"]
  LED158 = LED - 5mm [color="White (4500K)" current=20mA package="5 mm [THT]"]
  LED159 = LED - 5mm [color="White (4500K)" current=20mA package="5 mm [THT]"]
  LED160 = LED - 5mm [color="White (4500K)" current=20mA package="5 mm [THT]"]
  LED161 = LED - 5mm [color="White (4500K)" current=20mA package="5 mm [THT]"]
  LED162 = LED - 5mm [color="White (4500K)" current=20mA package="5 mm [THT]"]
  LED163 = LED - 5mm [color="White (4500K)" current=20mA package="5 mm [THT]"]
  LED164 = LED - 5mm [color="White (4500K)" current=20mA package="5 mm [THT]"]
  LED165 = LED - 5mm [color="White (4500K)" current=20mA package="5 mm [THT]"]
  LED166 = LED - 5mm [color="White (4500K)" current=20mA package="5 mm [THT]"]
  LED167 = LED - 5mm [color="White (4500K)" current=20mA package="5 mm [THT]"]
  LED168 = LED - 5mm [color="White (4500K)" current=20mA package="5 mm [THT]"]
  LED169 = LED - 5mm [color="White (4500K)" current=20mA package="5 mm [THT]"]
  LED170 = LED - 5mm [color="White (4500K)" current=20mA package="5 mm [THT]"]
  LED171 = LED - 5mm [color="White (4500K)" current=20mA package="5 mm [THT]"]
  LED172 = LED - 5mm [color="White (4500K)" current=20mA package="5 mm [THT]"]
  LED173 = LED - 5mm [color="White (4500K)" current=20mA package="5 mm [THT]"]
  LED174 = LED - 5mm [color="White (4500K)" current=20mA package="5 mm [THT]"]
  LED175 = LED - 5mm [color="White (4500K)" current=20mA package="5 mm [THT]"]
  LED176 = LED - 5mm [color="White (4500K)" current=20mA package="5 mm [THT]"]
  LED177 = LED - 5mm [color="White (4500K)" current=20mA package="5 mm [THT]"]
  LED178 = LED - 5mm [color="White (4500K)" current=20mA package="5 mm [THT]"]
  LED179 = LED - 5mm [color="White (4500K)" current=20mA package="5 mm [THT]"]
  LED180 = LED - 5mm [color="White (4500K)" current=20mA package="5 mm [THT]"]
  LED181 = LED - 5mm [color="White (4500K)" current=20mA package="5 mm [THT]"]
  LED182 = LED - 5mm [color="White (4500K)" current=20mA package="5 mm [THT]"]
  LED183 = LED - 5mm [color="White (4500K)" current=20mA package="5 mm [THT]"]
  LED184 = LED - 5mm [color="White (4500K)" current=20mA package="5 mm [THT]"]
  LED185 = LED - 5mm [color="White (4500K)" current=20mA package="5 mm [THT]"]
  LED186 = LED - 5mm [color="White (4500K)" current=20mA package="5 mm [THT]"]
  LED187 = LED - 5mm [color="White (4500K)" current=20mA package="5 mm [THT]"]
  LED188 = LED - 5mm [color="White (4500K)" current=20mA package="5 mm [THT]"]
  LED189 = LED - 5mm [color="White (4500K)" current=20mA package="5 mm [THT]"]
  LED190 = LED - 5mm [color="White (4500K)" current=20mA package="5 mm [THT]"]
  LED191 = LED - 5mm [color="White (4500K)" current=20mA package="5 mm [THT]"]
  LED192 = LED - 5mm [color="White (4500K)" current=20mA package="5 mm [THT]"]
  LED193 = LED - 5mm [color="White (4500K)" current=20mA package="5 mm [THT]"]
  LED194 = LED - 5mm [color="White (4500K)" current=20mA package="5 mm [THT]"]
  LED195 = LED - 5mm [color="White (4500K)" current=20mA package="5 mm [THT]"]
  LED196 = LED - 5mm [color="White (4500K)" current=20mA package="5 mm [THT]"]
  LED197 = LED - 5mm [color="White (4500K)" current=20mA package="5 mm [THT]"]
  LED198 = LED - 5mm [color="White (4500K)" current=20mA package="5 mm [THT]"]
  LED199 = LED - 5mm [color="White (4500K)" current=20mA package="5 mm [THT]"]
  LED200 = LED - 5mm [color="White (4500K)" current=20mA package="5 mm [THT]"]
  LED201 = LED - 5mm [color="White (4500K)" current=20mA package="5 mm [THT]"]
  LED202 = LED - 5mm [color="White (4500K)" current=20mA package="5 mm [THT]"]
  LED203 = LED - 5mm [color="White (4500K)" current=20mA package="5 mm [THT]"]
  LED204 = LED - 5mm [color="White (4500K)" current=20mA package="5 mm [THT]"]
  LED205 = LED - 5mm [color="White (4500K)" current=20mA package="5 mm [THT]"]
  LED206 = LED - 5mm [color="White (4500K)" current=20mA package="5 mm [THT]"]
  LED207 = LED - 5mm [color="White (4500K)" current=20mA package="5 mm [THT]"]
  LED208 = LED - 5mm [color="White (4500K)" current=20mA package="5 mm [THT]"]
  LED209 = LED - 5mm [color="White (4500K)" current=20mA package="5 mm [THT]"]
  LED210 = LED - 5mm [color="White (4500K)" current=20mA package="5 mm [THT]"]
  R67 = Resistor [tolerance=±5% resistance=300 package=THT]
  R68 = Resistor [tolerance=±5% resistance=300 package=THT]
  R69 = Resistor [tolerance=±5% resistance=300 package=THT]
  R70 = Resistor [tolerance=±5% resistance=300 package=THT]
  R71 = Resistor [tolerance=±5% resistance=300 package=THT]
  R72 = Resistor [tolerance=±5% resistance=300 package=THT]
  R73 = Resistor [tolerance=±5% resistance=300 package=THT]
  R74 = Resistor [tolerance=±5% resistance=300 package=THT]
  R75 = Resistor [tolerance=±5% resistance=300 package=THT]
  R76 = Resistor [tolerance=±5% resistance=300 package=THT]
  R77 = Resistor [tolerance=±5% resistance=300 package=THT]
  R78 = Resistor [tolerance=±5% resistance=300 package=THT]
  R79 = Resistor [tolerance=±5% resistance=300 package=THT]
  R80 = Resistor [tolerance=±5% resistance=300 package=THT]
  R81 = Resistor [tolerance=±5% resistance=300 package=THT]
  R82 = Resistor [tolerance=±5% resistance=300 package=THT]
  R83 = Resistor [tolerance=±5% resistance=300 package=THT]
  R84 = Resistor [tolerance=±5% resistance=300 package=THT]
  R85 = Resistor [tolerance=±5% resistance=300 package=THT]
  R86 = Resistor [tolerance=±5% resistance=300 package=THT]
  R87 = Resistor [tolerance=±5% resistance=300 package=THT]
  R88 = Resistor [tolerance=±5% resistance=300 package=THT]
  R89 = Resistor [tolerance=±5% resistance=300 package=THT]
  R90 = Resistor [tolerance=±5% resistance=1k package=THT]
  R91 = Resistor [tolerance=±5% resistance=1k package=THT]
  R92 = Resistor [tolerance=±5% resistance=1k package=THT]
  R93 = Resistor [tolerance=±5% resistance=1k package=THT]
  R94 = Resistor [tolerance=±5% resistance=1k package=THT]
  R95 = Resistor [tolerance=±5% resistance=1k package=THT]
  R96 = Resistor [tolerance=±5% resistance=1k package=THT]
  R97 = Resistor [tolerance=±5% resistance=1k package=THT]
  Q26 = NPN-Transistor [package="TO92 [THT]"]
  Q27 = NPN-Transistor [package="TO92 [THT]"]
  Q28 = NPN-Transistor [package="TO92 [THT]"]
  Q29 = NPN-Transistor [package="TO92 [THT]"]
  Q30 = NPN-Transistor [package="TO92 [THT]"]
  Q31 = NPN-Transistor [package="TO92 [THT]"]
  Q32 = NPN-Transistor [package="TO92 [THT]"]
  Q33 = NPN-Transistor [package="TO92 [THT]"]
  LED211 = LED - 5mm [color="White (4500K)" current=20mA package="5 mm [THT]"]
  LED212 = LED - 5mm [color="White (4500K)" current=20mA package="5 mm [THT]"]
  LED213 = LED - 5mm [color="White (4500K)" current=20mA package="5 mm [THT]"]
  LED214 = LED - 5mm [color="White (4500K)" current=20mA package="5 mm [THT]"]
  LED215 = LED - 5mm [color="White (4500K)" current=20mA package="5 mm [THT]"]
  LED216 = LED - 5mm [color="White (4500K)" current=20mA package="5 mm [THT]"]
  LED217 = LED - 5mm [color="White (4500K)" current=20mA package="5 mm [THT]"]
  LED218 = LED - 5mm [color="White (4500K)" current=20mA package="5 mm [THT]"]
  LED219 = LED - 5mm [color="White (4500K)" current=20mA package="5 mm [THT]"]
  LED220 = LED - 5mm [color="White (4500K)" current=20mA package="5 mm [THT]"]
  LED221 = LED - 5mm [color="White (4500K)" current=20mA package="5 mm [THT]"]
  LED222 = LED - 5mm [color="White (4500K)" current=20mA package="5 mm [THT]"]
  LED223 = LED - 5mm [color="White (4500K)" current=20mA package="5 mm [THT]"]
  LED224 = LED - 5mm [color="White (4500K)" current=20mA package="5 mm [THT]"]
  LED225 = LED - 5mm [color="White (4500K)" current=20mA package="5 mm [THT]"]
  LED226 = LED - 5mm [color="White (4500K)" current=20mA package="5 mm [THT]"]
  LED227 = LED - 5mm [color="White (4500K)" current=20mA package="5 mm [THT]"]
  LED228 = LED - 5mm [color="White (4500K)" current=20mA package="5 mm [THT]"]
  LED229 = LED - 5mm [color="White (4500K)" current=20mA package="5 mm [THT]"]
  LED230 = LED - 5mm [color="White (4500K)" current=20mA package="5 mm [THT]"]
  LED231 = LED - 5mm [color="White (4500K)" current=20mA package="5 mm [THT]"]
  LED232 = LED - 5mm [color="White (4500K)" current=20mA package="5 mm [THT]"]
  LED233 = LED - 5mm [color="White (4500K)" current=20mA package="5 mm [THT]"]
  LED234 = LED - 5mm [color="White (4500K)" current=20mA package="5 mm [THT]"]
  LED235 = LED - 5mm [color="White (4500K)" current=20mA package="5 mm [THT]"]
  LED236 = LED - 5mm [color="White (4500K)" current=20mA package="5 mm [THT]"]
  LED237 = LED - 5mm [color="White (4500K)" current=20mA package="5 mm [THT]"]
  LED238 = LED - 5mm [color="White (4500K)" current=20mA package="5 mm [THT]"]
  LED239 = LED - 5mm [color="White (4500K)" current=20mA package="5 mm [THT]"]
  LED240 = LED - 5mm [color="White (4500K)" current=20mA package="5 mm [THT]"]
  LED241 = LED - 5mm [color="White (4500K)" current=20mA package="5 mm [THT]"]
  LED242 = LED - 5mm [color="White (4500K)" current=20mA package="5 mm [THT]"]
  LED243 = LED - 5mm [color="White (4500K)" current=20mA package="5 mm [THT]"]
  LED244 = LED - 5mm [color="White (4500K)" current=20mA package="5 mm [THT]"]
  LED245 = LED - 5mm [color="White (4500K)" current=20mA package="5 mm [THT]"]
  LED246 = LED - 5mm [color="White (4500K)" current=20mA package="5 mm [THT]"]
  LED247 = LED - 5mm [color="White (4500K)" current=20mA package="5 mm [THT]"]
  LED248 = LED - 5mm [color="White (4500K)" current=20mA package="5 mm [THT]"]
  LED249 = LED - 5mm [color="White (4500K)" current=20mA package="5 mm [THT]"]
  LED250 = LED - 5mm [color="White (4500K)" current=20mA package="5 mm [THT]"]
  LED251 = LED - 5mm [color="White (4500K)" current=20mA package="5 mm [THT]"]
  LED252 = LED - 5mm [color="White (4500K)" current=20mA package="5 mm [THT]"]
  LED253 = LED - 5mm [color="White (4500K)" current=20mA package="5 mm [THT]"]
  LED254 = LED - 5mm [color="White (4500K)" current=20mA package="5 mm [THT]"]
  LED255 = LED - 5mm [color="White (4500K)" current=20mA package="5 mm [THT]"]
  LED256 = LED - 5mm [color="White (4500K)" current=20mA package="5 mm [THT]"]
  LED257 = LED - 5mm [color="White (4500K)" current=20mA package="5 mm [THT]"]
  LED258 = LED - 5mm [color="White (4500K)" current=20mA package="5 mm [THT]"]
  LED259 = LED - 5mm [color="White (4500K)" current=20mA package="5 mm [THT]"]
  LED260 = LED - 5mm [color="White (4500K)" current=20mA package="5 mm [THT]"]
  LED261 = LED - 5mm [color="White (4500K)" current=20mA package="5 mm [THT]"]
  LED262 = LED - 5mm [color="White (4500K)" current=20mA package="5 mm [THT]"]
  LED263 = LED - 5mm [color="White (4500K)" current=20mA package="5 mm [THT]"]
  LED264 = LED - 5mm [color="White (4500K)" current=20mA package="5 mm [THT]"]
  LED265 = LED - 5mm [color="White (4500K)" current=20mA package="5 mm [THT]"]
  LED266 = LED - 5mm [color="White (4500K)" current=20mA package="5 mm [THT]"]
  LED267 = LED - 5mm [color="White (4500K)" current=20mA package="5 mm [THT]"]
  LED268 = LED - 5mm [color="White (4500K)" current=20mA package="5 mm [THT]"]
  LED269 = LED - 5mm [color="White (4500K)" current=20mA package="5 mm [THT]"]
  LED270 = LED - 5mm [color="White (4500K)" current=20mA package="5 mm [THT]"]
  LED271 = LED - 5mm [color="White (4500K)" current=20mA package="5 mm [THT]"]
  LED272 = LED - 5mm [color="White (4500K)" current=20mA package="5 mm [THT]"]
  LED273 = LED - 5mm [color="White (4500K)" current=20mA package="5 mm [THT]"]
  LED274 = LED - 5mm [color="White (4500K)" current=20mA package="5 mm [THT]"]
  LED275 = LED - 5mm [color="White (4500K)" current=20mA package="5 mm [THT]"]
  LED276 = LED - 5mm [color="White (4500K)" current=20mA package="5 mm [THT]"]
  LED277 = LED - 5mm [color="White (4500K)" current=20mA package="5 mm [THT]"]
  R98 = Resistor [tolerance=±5% resistance=300 package=THT]
  R99 = Resistor [tolerance=±5% resistance=300 package=THT]
  R100 = Resistor [tolerance=±5% resistance=300 package=THT]
  R101 = Resistor [tolerance=±5% resistance=300 package=THT]
  R102 = Resistor [tolerance=±5% resistance=300 package=THT]
  R103 = Resistor [tolerance=±5% resistance=300 package=THT]
  R104 = Resistor [tolerance=±5% resistance=300 package=THT]
  R105 = Resistor [tolerance=±5% resistance=300 package=THT]
  R106 = Resistor [tolerance=±5% resistance=300 package=THT]
  R107 = Resistor [tolerance=±5% resistance=300 package=THT]
  R108 = Resistor [tolerance=±5% resistance=300 package=THT]
  R109 = Resistor [tolerance=±5% resistance=300 package=THT]
  R110 = Resistor [tolerance=±5% resistance=300 package=THT]
  R111 = Resistor [tolerance=±5% resistance=300 package=THT]
  R112 = Resistor [tolerance=±5% resistance=300 package=THT]
  R113 = Resistor [tolerance=±5% resistance=300 package=THT]
  R114 = Resistor [tolerance=±5% resistance=300 package=THT]
  R115 = Resistor [tolerance=±5% resistance=300 package=THT]
  R116 = Resistor [tolerance=±5% resistance=300 package=THT]
  R117 = Resistor [tolerance=±5% resistance=300 package=THT]
  R118 = Resistor [tolerance=±5% resistance=300 package=THT]
  R119 = Resistor [tolerance=±5% resistance=300 package=THT]
  R120 = Resistor [tolerance=±5% resistance=300 package=THT]
  R121 = Resistor [tolerance=±5% resistance=1k package=THT]
  R122 = Resistor [tolerance=±5% resistance=1k package=THT]
  R123 = Resistor [tolerance=±5% resistance=1k package=THT]
  R124 = Resistor [tolerance=±5% resistance=1k package=THT]
  R125 = Resistor [tolerance=±5% resistance=1k package=THT]
  R126 = Resistor [tolerance=±5% resistance=1k package=THT]
  R127 = Resistor [tolerance=±5% resistance=1k package=THT]
  R128 = Resistor [tolerance=±5% resistance=1k package=THT]

nets:
  GND: Q1.E, U1.GND, U1.OE, U2.GND, C1.0, C2.0, U3.GND, S1.Pin_3, S1.Pin_4, Q3.E, Q4.E, Q5.E, Q6.E, Q7.E, Q8.E, Q9.E, U4.GND, U4.OE, C3.0, U5.GND, U5.OE, U6.GND, U6.OE, IC1.pin1, Q10.E, Q11.E, Q12.E, Q13.E, Q14.E, Q15.E, Q16.E, Q17.E, Q18.E, Q19.E, Q20.E, Q21.E, Q22.E, Q23.E, Q24.E, Q25.E, Q26.E, Q27.E, Q28.E, Q29.E, Q30.E, Q31.E, Q32.E, Q33.E
  N1: Q1.B, R4.Pin_1
  N2: Q1.C, R1.Pin_0, R2.Pin_0, R3.Pin_0
  N3: U1.Q1, R11.Pin_0
  N4: U1.Q2, R15.Pin_0
  N5: U1.Q3, R31.Pin_0
  N6: U1.Q4, R32.Pin_0
  N7: U1.Q5, R33.Pin_0
  N8: U1.Q6, R34.Pin_0
  N9: U1.Q7, R35.Pin_0
  N10: U1.Q7', U4.DS
  VCC: U1.MR, U1.VCC, U2.VCC, U2.AVCC, U2.AREF, U3.output_voltage, R5.Pin_0, U4.MR, U4.VCC, U5.MR, U5.VCC, U6.MR, U6.VCC, IC1.pin2
  N11: U1.SH_CP, U2.D12, U4.SH_CP, U5.SH_CP, U6.SH_CP
  N12: U1.ST_CP, U2.D8, U4.ST_CP, C3.1, U5.ST_CP, U6.ST_CP
  N13: U1.DS, U2.D11_(PWM)
  N14: U1.Q0, R4.Pin_0
  N15: LED2.cathode, R1.Pin_1
  N16: LED2.anode, LED3.cathode
  N17: LED3.anode, LED4.cathode
  12V: LED4.anode, LED7.anode, LED8.anode, U3.input_voltage, LED18.anode, LED20.anode, LED22.anode, LED27.anode, LED29.anode, LED31.anode, LED34.anode, LED37.anode, LED40.anode, LED43.anode, LED46.anode, LED49.anode, LED52.anode, LED55.anode, LED58.anode, LED61.anode, LED64.anode, LED67.anode, LED72.anode, LED73.anode, LED80.anode, LED82.anode, LED83.anode, LED89.anode, LED91.anode, LED92.anode, LED95.anode, LED97.anode, LED98.anode, LED99.anode, LED100.anode, LED107.anode, LED111.anode, LED114.anode, LED117.anode, LED118.anode, LED119.anode, LED120.anode, LED125.anode, LED135.anode, LED136.anode, LED140.anode, LED143.anode, LED144.anode, LED146.anode, LED152.anode, LED154.anode, LED160.anode, LED166.anode, LED167.anode, LED169.anode, LED174.anode, LED179.anode, LED182.anode, LED185.anode, LED187.anode, LED188.anode, LED190.anode, LED195.anode, LED197.anode, LED201.anode, LED202.anode, LED204.anode, LED208.anode, LED209.anode, LED210.anode, LED211.anode, LED213.anode, LED219.anode, LED221.anode, LED227.anode, LED233.anode, LED234.anode, LED236.anode, LED241.anode, LED246.anode, LED249.anode, LED252.anode, LED254.anode, LED255.anode, LED257.anode, LED262.anode, LED264.anode, LED268.anode, LED269.anode, LED271.anode, LED275.anode, LED276.anode, LED277.anode
  N18: LED5.cathode, R2.Pin_1
  N19: LED5.anode, LED6.cathode
  N20: LED6.anode, LED7.cathode
  N21: LED8.cathode, LED10.anode
  N22: LED9.cathode, R3.Pin_1
  N23: LED9.anode, LED10.cathode
  N24: U2.RESET, S1.Pin_1, S1.Pin_2, R5.Pin_1
  N25: U2.XLAT1, XTAL1.pin_0, C1.1
  N26: U2.XLAT2, XTAL1.pin_1, C2.1
  N27: U2.A4, IC1.pin8
  N28: U2.A5, IC1.pin7
  N29: Q3.B, R11.Pin_1
  N30: Q3.C, R8.Pin_0, R9.Pin_0, R10.Pin_0
  N31: LED15.cathode, LED19.anode
  N32: LED15.anode, LED22.cathode
  N33: LED16.cathode, R10.Pin_1
  N34: LED16.anode, LED21.cathode
  N35: LED17.cathode, LED23.anode
  N36: LED17.anode, LED20.cathode
  N37: LED18.cathode, LED21.anode
  N38: LED19.cathode, R9.Pin_1
  N39: LED23.cathode, R8.Pin_1
  N40: Q4.B, R15.Pin_1
  N41: Q4.C, R12.Pin_0, R13.Pin_0, R14.Pin_0
  N42: LED24.cathode, LED28.anode
  N43: LED24.anode, LED31.cathode
  N44: LED25.cathode, R14.Pin_1
  N45: LED25.anode, LED30.cathode
  N46: LED26.cathode, LED32.anode
  N47: LED26.anode, LED29.cathode
  N48: LED27.cathode, LED30.anode
  N49: LED28.cathode, R13.Pin_1
  N50: LED32.cathode, R12.Pin_1
  N51: Q5.B, R31.Pin_1
  N52: Q5.C, R16.Pin_0, R17.Pin_0, R18.Pin_0
  N53: LED33.cathode, LED39.anode
  N54: LED33.anode, LED40.cathode
  N55: LED34.cathode, LED38.anode
  N56: LED35.cathode, R18.Pin_1
  N57: LED35.anode, LED41.cathode
  N58: LED36.cathode, R16.Pin_1
  N59: LED36.anode, LED38.cathode
  N60: LED37.cathode, LED41.anode
  N61: LED39.cathode, R17.Pin_1
  N62: Q6.B, R32.Pin_1
  N63: Q6.C, R19.Pin_0, R20.Pin_0, R21.Pin_0
  N64: LED42.cathode, LED48.anode
  N65: LED42.anode, LED49.cathode
  N66: LED43.cathode, LED47.anode
  N67: LED44.cathode, R21.Pin_1
  N68: LED44.anode, LED50.cathode
  N69: LED45.cathode, R19.Pin_1
  N70: LED45.anode, LED47.cathode
  N71: LED46.cathode, LED50.anode
  N72: LED48.cathode, R20.Pin_1
  N73: Q7.B, R33.Pin_1
  N74: Q7.C, R22.Pin_0, R23.Pin_0, R24.Pin_0
  N75: LED51.cathode, LED57.anode
  N76: LED51.anode, LED58.cathode
  N77: LED52.cathode, LED56.anode
  N78: LED53.cathode, R24.Pin_1
  N79: LED53.anode, LED59.cathode
  N80: LED54.cathode, R22.Pin_1
  N81: LED54.anode, LED56.cathode
  N82: LED55.cathode, LED59.anode
  N83: LED57.cathode, R23.Pin_1
  N84: Q8.B, R34.Pin_1
  N85: Q8.C, R25.Pin_0, R26.Pin_0, R27.Pin_0
  N86: LED60.cathode, LED66.anode
  N87: LED60.anode, LED67.cathode
  N88: LED61.cathode, LED65.anode
  N89: LED62.cathode, R27.Pin_1
  N90: LED62.anode, LED68.cathode
  N91: LED63.cathode, R25.Pin_1
  N92: LED63.anode, LED65.cathode
  N93: LED64.cathode, LED68.anode
  N94: LED66.cathode, R26.Pin_1
  N95: Q9.B, R35.Pin_1
  N96: Q9.C, R29.Pin_0, R30.Pin_0
  N97: LED72.cathode, LED74.anode
  N98: LED73.cathode, LED76.anode
  N99: LED74.cathode, R30.Pin_1
  N100: LED76.cathode, R29.Pin_1
  N101: U4.Q1, R43.Pin_0
  N102: U4.Q2, R62.Pin_0
  N103: U4.Q3, R64.Pin_0
  N104: U4.Q4, R63.Pin_0
  N105: U4.Q5, R66.Pin_0
  N106: U4.Q6, R65.Pin_0
  N107: U4.Q7, R61.Pin_0
  N108: U4.Q7', U5.DS
  N109: U4.Q0, R39.Pin_0
  N110: U5.Q1, R91.Pin_0
  N111: U5.Q2, R97.Pin_0
  N112: U5.Q3, R95.Pin_0
  N113: U5.Q4, R93.Pin_0
  N114: U5.Q5, R90.Pin_0
  N115: U5.Q6, R92.Pin_0
  N116: U5.Q7, R96.Pin_0
  N117: U5.Q7', U6.DS
  N118: U5.Q0, R94.Pin_0
  N119: U6.Q1, R122.Pin_0
  N120: U6.Q2, R128.Pin_0
  N121: U6.Q3, R126.Pin_0
  N122: U6.Q4, R124.Pin_0
  N123: U6.Q5, R121.Pin_0
  N124: U6.Q6, R123.Pin_0
  N125: U6.Q7, R127.Pin_0
  N126: U6.Q0, R125.Pin_0
  N127: Q10.B, R39.Pin_1
  N128: Q10.C, R36.Pin_0, R37.Pin_0, R38.Pin_0
  N129: LED77.cathode, LED81.anode
  N130: LED77.anode, LED83.cathode
  N131: LED78.cathode, R36.Pin_1
  N132: LED78.anode, LED84.cathode
  N133: LED79.cathode, LED85.anode
  N134: LED79.anode, LED82.cathode
  N135: LED80.cathode, LED84.anode
  N136: LED81.cathode, R37.Pin_1
  N137: LED85.cathode, R38.Pin_1
  N138: Q11.B, R43.Pin_1
  N139: Q11.C, R40.Pin_0, R41.Pin_0, R42.Pin_0
  N140: LED86.cathode, LED90.anode
  N141: LED86.anode, LED92.cathode
  N142: LED87.cathode, R40.Pin_1
  N143: LED87.anode, LED93.cathode
  N144: LED88.cathode, LED94.anode
  N145: LED88.anode, LED91.cathode
  N146: LED89.cathode, LED93.anode
  N147: LED90.cathode, R41.Pin_1
  N148: LED94.cathode, R42.Pin_1
  N149: Q12.B, R64.Pin_1
  N150: Q12.C, R44.Pin_0, R49.Pin_0, R59.Pin_0
  N151: Q13.B, R63.Pin_1
  N152: Q13.C, R48.Pin_0, R54.Pin_0, R56.Pin_0
  N153: Q14.B, R61.Pin_1
  N154: Q14.C, R45.Pin_0, R60.Pin_0
  N155: Q15.B, R65.Pin_1
  N156: Q15.C, R50.Pin_0, R51.Pin_0, R57.Pin_0
  N157: Q16.B, R62.Pin_1
  N158: Q16.C, R46.Pin_0, R52.Pin_0, R58.Pin_0
  N159: Q17.B, R66.Pin_1
  N160: Q17.C, R47.Pin_0, R53.Pin_0, R55.Pin_0
  N161: LED95.cathode, LED103.anode
  N162: LED96.cathode, LED129.anode
  N163: LED96.anode, LED98.cathode
  N164: LED97.cathode, LED106.anode
  N165: LED99.cathode, LED110.anode
  N166: LED100.cathode, LED121.anode
  N167: LED101.cathode, LED116.anode
  N168: LED101.anode, LED117.cathode
  N169: LED102.cathode, R53.Pin_1
  N170: LED102.anode, LED121.cathode
  N171: LED103.cathode, LED124.anode
  N172: LED104.cathode, R56.Pin_1
  N173: LED104.anode, LED109.cathode
  N174: LED105.cathode, R48.Pin_1
  N175: LED105.anode, LED141.cathode
  N176: LED106.cathode, LED128.anode
  N177: LED107.cathode, LED109.anode
  N178: LED108.cathode, R59.Pin_1
  N179: LED108.anode, LED142.cathode
  N180: LED110.cathode, R45.Pin_1
  N181: LED111.cathode, LED132.anode
  N182: LED112.cathode, LED138.anode
  N183: LED112.anode, LED140.cathode
  N184: LED113.cathode, R50.Pin_1
  N185: LED113.anode, LED132.cathode
  N186: LED114.cathode, LED142.anode
  N187: LED115.cathode, R52.Pin_1
  N188: LED115.anode, LED131.cathode
  N189: LED116.cathode, R57.Pin_1
  N190: LED118.cathode, LED141.anode
  N191: LED119.cathode, LED137.anode
  N192: LED120.cathode, LED127.anode
  N193: LED122.cathode, R58.Pin_1
  N194: LED122.anode, LED130.cathode
  N195: LED123.cathode, R47.Pin_1
  N196: LED123.anode, LED127.cathode
  N197: LED124.cathode, R44.Pin_1
  N198: LED125.cathode, LED131.anode
  N199: LED126.cathode, R55.Pin_1
  N200: LED126.anode, LED133.cathode
  N201: LED128.cathode, R54.Pin_1
  N202: LED129.cathode, R51.Pin_1
  N203: LED130.anode, LED143.cathode
  N204: LED133.anode, LED135.cathode
  N205: LED134.cathode, R46.Pin_1
  N206: LED134.anode, LED137.cathode
  N207: LED136.cathode, LED139.anode
  N208: LED138.cathode, R49.Pin_1
  N209: LED139.cathode, R60.Pin_1
  N210: Q18.B, R90.Pin_1
  N211: Q18.C, R72.Pin_0, R77.Pin_0, R87.Pin_0
  N212: Q19.B, R91.Pin_1
  N213: Q19.C, R69.Pin_0, R70.Pin_0, R80.Pin_0
  N214: Q20.B, R95.Pin_1
  N215: Q20.C, R81.Pin_0, R82.Pin_0, R85.Pin_0
  N216: Q21.B, R96.Pin_1
  N217: Q21.C, R83.Pin_0, R84.Pin_0
  N218: Q22.B, R92.Pin_1
  N219: Q22.C, R71.Pin_0, R76.Pin_0, R88.Pin_0
  N220: Q23.B, R93.Pin_1
  N221: Q23.C, R67.Pin_0, R78.Pin_0, R86.Pin_0
  N222: Q24.B, R97.Pin_1
  N223: Q24.C, R73.Pin_0, R75.Pin_0, R89.Pin_0
  N224: Q25.B, R94.Pin_1
  N225: Q25.C, R68.Pin_0, R74.Pin_0, R79.Pin_0
  N226: LED144.cathode, LED175.anode
  N227: LED145.cathode, R86.Pin_1
  N228: LED145.anode, LED165.cathode
  N229: LED146.cathode, LED157.anode
  N230: LED147.cathode, LED158.anode
  N231: LED147.anode, LED154.cathode
  N232: LED148.cathode, LED203.anode
  N233: LED148.anode, LED152.cathode
  N234: LED149.cathode, R68.Pin_1
  N235: LED149.anode, LED184.cathode
  N236: LED150.cathode, R83.Pin_1
  N237: LED150.anode, LED209.cathode
  N238: LED151.cathode, R71.Pin_1
  N239: LED151.anode, LED177.cathode
  N240: LED153.cathode, R89.Pin_1
  N241: LED153.anode, LED172.cathode
  N242: LED155.cathode, R69.Pin_1
  N243: LED155.anode, LED162.cathode
  N244: LED156.cathode, LED183.anode
  N245: LED156.anode, LED208.cathode
  N246: LED157.cathode, LED196.anode
  N247: LED158.cathode, R73.Pin_1
  N248: LED159.cathode, LED173.anode
  N249: LED159.anode, LED179.cathode
  N250: LED160.cathode, LED184.anode
  N251: LED161.cathode, LED164.anode
  N252: LED161.anode, LED202.cathode
  N253: LED162.anode, LED167.cathode
  N254: LED163.cathode, R85.Pin_1
  N255: LED163.anode, LED181.cathode
  N256: LED164.cathode, R80.Pin_1
  N257: LED165.anode, LED182.cathode
  N258: LED166.cathode, LED171.anode
  N259: LED168.cathode, R82.Pin_1
  N260: LED168.anode, LED178.cathode
  N261: LED169.cathode, LED191.anode
  N262: LED170.cathode, LED176.anode
  N263: LED170.anode, LED210.cathode
  N264: LED171.cathode, LED205.anode
  N265: LED172.anode, LED185.cathode
  N266: LED173.cathode, R72.Pin_1
  N267: LED174.cathode, LED181.anode
  N268: LED175.cathode, LED186.anode
  N269: LED176.cathode, R76.Pin_1
  N270: LED177.anode, LED201.cathode
  N271: LED178.anode, LED195.cathode
  N272: LED180.cathode, LED207.anode
  N273: LED180.anode, LED190.cathode
  N274: LED183.cathode, R74.Pin_1
  N275: LED186.cathode, R70.Pin_1
  N276: LED187.cathode, LED192.anode
  N277: LED188.cathode, LED193.anode
  N278: LED189.cathode, R67.Pin_1
  N279: LED189.anode, LED199.cathode
  N280: LED191.cathode, LED200.anode
  N281: LED192.cathode, LED206.anode
  N282: LED193.cathode, R84.Pin_1
  N283: LED194.cathode, LED198.anode
  N284: LED194.anode, LED204.cathode
  N285: LED196.cathode, R77.Pin_1
  N286: LED197.cathode, LED199.anode
  N287: LED198.cathode, R88.Pin_1
  N288: LED200.cathode, R79.Pin_1
  N289: LED203.cathode, R87.Pin_1
  N290: LED205.cathode, R78.Pin_1
  N291: LED206.cathode, R81.Pin_1
  N292: LED207.cathode, R75.Pin_1
  N293: Q26.B, R121.Pin_1
  N294: Q26.C, R103.Pin_0, R108.Pin_0, R118.Pin_0
  N295: Q27.B, R122.Pin_1
  N296: Q27.C, R100.Pin_0, R101.Pin_0, R111.Pin_0
  N297: Q28.B, R126.Pin_1
  N298: Q28.C, R112.Pin_0, R113.Pin_0, R116.Pin_0
  N299: Q29.B, R127.Pin_1
  N300: Q29.C, R114.Pin_0, R115.Pin_0
  N301: Q30.B, R123.Pin_1
  N302: Q30.C, R102.Pin_0, R107.Pin_0, R119.Pin_0
  N303: Q31.B, R124.Pin_1
  N304: Q31.C, R98.Pin_0, R109.Pin_0, R117.Pin_0
  N305: Q32.B, R128.Pin_1
  N306: Q32.C, R104.Pin_0, R106.Pin_0, R120.Pin_0
  N307: Q33.B, R125.Pin_1
  N308: Q33.C, R99.Pin_0, R105.Pin_0, R110.Pin_0
  N309: LED211.cathode, LED242.anode
  N310: LED212.cathode, R117.Pin_1
  N311: LED212.anode, LED232.cathode
  N312: LED213.cathode, LED224.anode
  N313: LED214.cathode, LED225.anode
  N314: LED214.anode, LED221.cathode
  N315: LED215.cathode, LED270.anode
  N316: LED215.anode, LED219.cathode
  N317: LED216.cathode, R99.Pin_1
  N318: LED216.anode, LED251.cathode
  N319: LED217.cathode, R114.Pin_1
  N320: LED217.anode, LED276.cathode
  N321: LED218.cathode, R102.Pin_1
  N322: LED218.anode, LED244.cathode
  N323: LED220.cathode, R120.Pin_1
  N324: LED220.anode, LED239.cathode
  N325: LED222.cathode, R100.Pin_1
  N326: LED222.anode, LED229.cathode
  N327: LED223.cathode, LED250.anode
  N328: LED223.anode, LED275.cathode
  N329: LED224.cathode, LED263.anode
  N330: LED225.cathode, R104.Pin_1
  N331: LED226.cathode, LED240.anode
  N332: LED226.anode, LED246.cathode
  N333: LED227.cathode, LED251.anode
  N334: LED228.cathode, LED231.anode
  N335: LED228.anode, LED269.cathode
  N336: LED229.anode, LED234.cathode
  N337: LED230.cathode, R116.Pin_1
  N338: LED230.anode, LED248.cathode
  N339: LED231.cathode, R111.Pin_1
  N340: LED232.anode, LED249.cathode
  N341: LED233.cathode, LED238.anode
  N342: LED235.cathode, R113.Pin_1
  N343: LED235.anode, LED245.cathode
  N344: LED236.cathode, LED258.anode
  N345: LED237.cathode, LED243.anode
  N346: LED237.anode, LED277.cathode
  N347: LED238.cathode, LED272.anode
  N348: LED239.anode, LED252.cathode
  N349: LED240.cathode, R103.Pin_1
  N350: LED241.cathode, LED248.anode
  N351: LED242.cathode, LED253.anode
  N352: LED243.cathode, R107.Pin_1
  N353: LED244.anode, LED268.cathode
  N354: LED245.anode, LED262.cathode
  N355: LED247.cathode, LED274.anode
  N356: LED247.anode, LED257.cathode
  N357: LED250.cathode, R105.Pin_1
  N358: LED253.cathode, R101.Pin_1
  N359: LED254.cathode, LED259.anode
  N360: LED255.cathode, LED260.anode
  N361: LED256.cathode, R98.Pin_1
  N362: LED256.anode, LED266.cathode
  N363: LED258.cathode, LED267.anode
  N364: LED259.cathode, LED273.anode
  N365: LED260.cathode, R115.Pin_1
  N366: LED261.cathode, LED265.anode
  N367: LED261.anode, LED271.cathode
  N368: LED263.cathode, R108.Pin_1
  N369: LED264.cathode, LED266.anode
  N370: LED265.cathode, R119.Pin_1
  N371: LED267.cathode, R110.Pin_1
  N372: LED270.cathode, R118.Pin_1
  N373: LED272.cathode, R109.Pin_1
  N374: LED273.cathode, R112.Pin_1
  N375: LED274.cathode, R106.Pin_1

notes:
  (atmega328)
  Latch
  Data
  Clock
  ________
  A - Q0
  B - Q1
  C - Q2
  D - Q3
  E - Q4
  F - Q5
  G - Q6
  .
  H - Q7
  SCL
  SDA
